// Logisim project Single-Cycle_ARM_Proc.circ as structural Verilog: 15 circuits, main circuit main
module main (
  input  [1:0] _3_sum_array,
  input  clr
);

  wire clock_1_out, control_unit_1_alusrc, control_unit_1_bl, control_unit_1_bx, control_unit_1_memtoreg,
       control_unit_1_memwrite, control_unit_1_mov, control_unit_1_pcsrc, control_unit_1_regwrite,
       regid_1_bl_2, regid_1_bx_2;
  wire [1:0] control_unit_1_alucontrol, control_unit_1_immsrc, control_unit_1_regsrc;
  wire [3:0] alu_1_alu_flags, regid_1_a1, regid_1_a2, regid_1_a3;
  wire [31:0] alu_1_aluresult, alu_1_aout, data_memory_1_rd, extender_1_extimm, instruction_memory_1_rd,
       multiplexer_1_out, multiplexer_2_out, multiplexer_3_out, multiplexer_4_out, multiplexer_5_out,
       multiplexer_6_out, PC, pcplus_1_pcplus4, pcplus_1_pcplus8, register_file_1_r0, register_file_1_r1,
       register_file_1_r2, register_file_1_r3, register_file_1_r4, register_file_1_r5, register_file_1_r6,
       register_file_1_r7, register_file_1_r8, register_file_1_r9, register_file_1_r10, register_file_1_r11,
       register_file_1_r12, register_file_1_r13, register_file_1_r14, register_file_1_rd1,
       register_file_1_rd2;

  Clock clock_1 (.out(clock_1_out));
  Multiplexer #(.width(32), .disabled(0), .enable("false")) multiplexer_1 (
    .in0(pcplus_1_pcplus4), .in1(multiplexer_3_out), .out(multiplexer_1_out), .sel(control_unit_1_pcsrc));
  Register #(.width(32)) u_PC (.D(multiplexer_1_out), .Q(PC), .clk(clock_1_out), .clr(clr));  // open: en
  Instruction_Memory instruction_memory_1 (.A(PC), .RD(instruction_memory_1_rd), .in_1(_3_sum_array));
  PCPlus pcplus_1 (.PC(PC), .PCPlus4(pcplus_1_pcplus4), .PCPlus8(pcplus_1_pcplus8));
  Control_Unit control_unit_1 (
    .Cond(instruction_memory_1_rd[31:28]), .Op(instruction_memory_1_rd[27:26]),
    .Funct(instruction_memory_1_rd[25:20]), .RD(instruction_memory_1_rd[15:12]),
    .PCSrc(control_unit_1_pcsrc), .MemtoReg(control_unit_1_memtoreg), .MemWrite(control_unit_1_memwrite),
    .ALUControl(control_unit_1_alucontrol), .ALUSrc(control_unit_1_alusrc), .ImmSrc(control_unit_1_immsrc),
    .RegWrite(control_unit_1_regwrite), .RegSrc(control_unit_1_regsrc), .ALUFlags(alu_1_alu_flags),
    .clk(clock_1_out), .BX(control_unit_1_bx), .BL(control_unit_1_bl),
    .BXRange(instruction_memory_1_rd[27:4]), .MOV(control_unit_1_mov), .clr(clr));
  RegID regid_1 (
    .RN(instruction_memory_1_rd[19:16]), .RM(instruction_memory_1_rd[3:0]),
    .RD(instruction_memory_1_rd[15:12]), .A1(regid_1_a1), .A2(regid_1_a2), .A3(regid_1_a3),
    .BX(control_unit_1_bx), .BL(control_unit_1_bl), .RegSrc(control_unit_1_regsrc), .BL_2(regid_1_bl_2),
    .BX_2(regid_1_bx_2));
  Multiplexer #(.width(32), .disabled(0), .enable("false")) multiplexer_2 (
    .in0(multiplexer_6_out), .in1(pcplus_1_pcplus4), .out(multiplexer_2_out), .sel(regid_1_bl_2));
  Multiplexer #(.width(32), .disabled(0), .enable("false")) multiplexer_3 (
    .in0(multiplexer_6_out), .in1(alu_1_aout), .out(multiplexer_3_out), .sel(regid_1_bx_2));
  Register_File register_file_1 (
    .clk(clock_1_out), .A3(regid_1_a3), .WD3(multiplexer_2_out), .R15(pcplus_1_pcplus8),
    .WE3(control_unit_1_regwrite), .R0(register_file_1_r0), .R1(register_file_1_r1), .R2(register_file_1_r2),
    .R3(register_file_1_r3), .R4(register_file_1_r4), .R5(register_file_1_r5), .R6(register_file_1_r6),
    .R7(register_file_1_r7), .R8(register_file_1_r8), .R9(register_file_1_r9), .R10(register_file_1_r10),
    .R11(register_file_1_r11), .R12(register_file_1_r12), .R13(register_file_1_r13),
    .R14(register_file_1_r14), .clr(clr), .RD1(register_file_1_rd1), .A1(regid_1_a1),
    .RD2(register_file_1_rd2), .A2(regid_1_a2));
  Extender extender_1 (
    ._23_0(instruction_memory_1_rd[23:0]), .ImmSrc(control_unit_1_immsrc), .ExtImm(extender_1_extimm));
  Multiplexer #(.width(32), .disabled(0), .enable("false")) multiplexer_4 (
    .in0(register_file_1_rd1), .in1({32{1'b0}}), .out(multiplexer_4_out), .sel(control_unit_1_mov));
  Multiplexer #(.width(32), .disabled(0), .enable("false")) multiplexer_5 (
    .in0(register_file_1_rd2), .in1(extender_1_extimm), .out(multiplexer_5_out), .sel(control_unit_1_alusrc));
  ALU alu_1 (
    .ALU_Flags(alu_1_alu_flags), .Aout(alu_1_aout), .A(multiplexer_4_out), .B(multiplexer_5_out),
    .ALU_Control(control_unit_1_alucontrol), .ALUResult(alu_1_aluresult));
  Data_Memory data_memory_1 (
    .A(alu_1_aluresult), .clk(clock_1_out), .WE(control_unit_1_memwrite), .clr(clr), .RD(data_memory_1_rd),
    .WD(register_file_1_rd2));
  Multiplexer #(.width(32), .disabled(0), .enable("false")) multiplexer_6 (
    .in0(alu_1_aluresult), .in1(data_memory_1_rd), .out(multiplexer_6_out), .sel(control_unit_1_memtoreg));
  // Probe on register_file_1_r0
  // Probe on register_file_1_r1
  // Probe on register_file_1_r2
  // Probe on register_file_1_r3
  // Probe on register_file_1_r4
  // Probe on register_file_1_r5
  // Probe on register_file_1_r6
  // Probe on register_file_1_r7
  // Probe on register_file_1_r8
  // Probe on register_file_1_r9
  // Probe on register_file_1_r10
  // Probe on register_file_1_r11
  // Probe on register_file_1_r12
  // Probe on register_file_1_r13
  // Probe on register_file_1_r14
  // Probe on PC

  // Notes on the sheet:
  //   0-fib iter (10)
  //   1-fib rec (10)
  //   2-find max
endmodule

module Control_Unit (
  input  clr,
  input  clk,
  input  [3:0] Cond,
  input  [3:0] ALUFlags,
  input  [23:0] BXRange,
  input  [1:0] Op,
  input  [5:0] Funct,
  input  [3:0] RD,
  output PCSrc,
  output RegWrite,
  output MemWrite,
  output BX,
  output MOV,
  output MemtoReg,
  output ALUSrc,
  output [1:0] ImmSrc,
  output [1:0] RegSrc,
  output [1:0] ALUControl,
  output BL
);

  wire decoder_1_bx, decoder_1_cmp, decoder_1_memw, decoder_1_mov, decoder_1_pcs, decoder_1_regw;
  wire [1:0] decoder_1_flagw;

  Decoder decoder_1 (
    .Op(Op), .Funct(Funct), .Rd(RD), .FlagW(decoder_1_flagw), .PCS(decoder_1_pcs), .RegW(decoder_1_regw),
    .MemW(decoder_1_memw), .MemtoReg(MemtoReg), .ALUSrc(ALUSrc), .ImmSrc(ImmSrc), .RegSrc(RegSrc),
    .ALUControl(ALUControl), .CMP(decoder_1_cmp), .MOV(decoder_1_mov), .BL(BL), .BX(decoder_1_bx),
    .BXRange(BXRange));
  Conditional_Logic conditional_logic_1 (
    .Cond(Cond), .ALUFlags(ALUFlags), .PCSrc(PCSrc), .RegWrite(RegWrite), .MemWrite(MemWrite), .clk(clk),
    .FlagW(decoder_1_flagw), .PCS(decoder_1_pcs), .RegW(decoder_1_regw), .MemW(decoder_1_memw),
    .CMP(decoder_1_cmp), .MOV(decoder_1_mov), .MOV_2(MOV), .clr(clr), .BX(decoder_1_bx), .BX_2(BX));
endmodule

module Conditional_Logic (
  input  PCS,
  input  BX,
  input  CMP,
  input  RegW,
  input  MemW,
  input  MOV,
  input  [1:0] FlagW,
  input  [3:0] Cond,
  input  [3:0] ALUFlags,
  input  clk,
  input  clr,
  output PCSrc,
  output BX_2,
  output RegWrite,
  output MemWrite,
  output MOV_2
);

  wire and_1_out, and_2_out, and_3_out, condition_check_1_condex;
  wire [1:0] register_1_q, register_2_q;

  and and_1 (and_1_out, FlagW[0], condition_check_1_condex);
  and and_2 (and_2_out, FlagW[1], condition_check_1_condex);
  Register #(.width(2)) register_1 (.D(ALUFlags[3:2]), .en(and_2_out), .Q(register_1_q), .clk(clk), .clr(clr));
  Register #(.width(2)) register_2 (.D(ALUFlags[1:0]), .en(and_1_out), .Q(register_2_q), .clk(clk), .clr(clr));
  Condition_Check condition_check_1 (
    .CondEx(condition_check_1_condex), .Cond(Cond), .NZ(register_1_q), .VC(register_2_q));
  and and_3 (and_3_out, PCS, condition_check_1_condex);
  and and_4 (BX_2, BX, condition_check_1_condex);
  and and_5 (RegWrite, ~CMP, RegW, condition_check_1_condex);  // AND_Gate
  and and_6 (MemWrite, MemW, condition_check_1_condex);
  and and_7 (MOV_2, MOV, condition_check_1_condex);
  or or_1 (PCSrc, and_3_out, BX_2);
endmodule

module Condition_Check (
  input  [3:0] Cond,
  input  [1:0] NZ,
  input  [1:0] VC,
  output CondEx
);

  wire AL_out, and_1_out, EQ_out, GT_out, xor_1_out;

  xor xor_1 (xor_1_out, NZ[1], VC[1]);
  and and_1 (and_1_out, ~xor_1_out, ~NZ[0]);  // AND_Gate
  and GT (GT_out, ~and_1_out, Cond[3], Cond[2], ~Cond[1], ~Cond[0]);  // AND_Gate
  and EQ (EQ_out, ~Cond[3], ~Cond[2], ~Cond[1], ~Cond[0], NZ[0]);  // AND_Gate
  and AL (AL_out, ~Cond[0], Cond[1], Cond[2], Cond[3]);  // AND_Gate
  or or_1 (CondEx, GT_out, EQ_out, AL_out);
endmodule

module Decoder (
  input  [3:0] Rd,
  input  [23:0] BXRange,
  input  [1:0] Op,
  input  [5:0] Funct,
  output PCS,
  output RegW,
  output MemW,
  output MemtoReg,
  output ALUSrc,
  output [1:0] ImmSrc,
  output [1:0] RegSrc,
  output BL,
  output BX,
  output [1:0] ALUControl,
  output [1:0] FlagW,
  output CMP,
  output MOV
);

  wire main_decoder_1_aluop, main_decoder_1_branch;

  Main_Decoder main_decoder_1 (
    .Op(Op), .RegW(RegW), .AluSrc(ALUSrc), .ImmSrc(ImmSrc), .RegSrc(RegSrc), .Branch(main_decoder_1_branch),
    .Funct(Funct), .ALUop(main_decoder_1_aluop), .MemtoReg(MemtoReg), .MemW(MemW), .BXRange(BXRange),
    .BL(BL), .BX(BX));
  ALU_Decoder alu_decoder_1 (
    .Funct(Funct[4:0]), .ALU_Op(main_decoder_1_aluop), .MOV(MOV), .ALU_Control(ALUControl), .FlagW(FlagW),
    .CMP(CMP));
  PC_Logic pc_logic_1 (.Rd(Rd), .PCS(PCS), .Branch(main_decoder_1_branch), .RegW(RegW));
endmodule

module PC_Logic (
  input  [3:0] Rd,
  input  RegW,
  input  Branch,
  output PCS
);

  wire and_1_out, comparator_1_eq;

  Comparator #(.width(4)) comparator_1 (.a(4'b1111), .b(Rd), .eq(comparator_1_eq));  // open: gt, lt
  and and_1 (and_1_out, comparator_1_eq, RegW);
  or or_1 (PCS, and_1_out, Branch);
endmodule

module Main_Decoder (
  input  [23:0] BXRange,
  input  [1:0] Op,
  input  [5:0] Funct,
  output BL,
  output Branch,
  output MemtoReg,
  output MemW,
  output [1:0] RegSrc,
  output [1:0] ImmSrc,
  output RegW,
  output AluSrc,
  output ALUop,
  output BX
);

  wire DPI_out, DPR_out;

  Comparator #(.width(24)) comparator_1 (.a(24'h12fff1), .b(BXRange), .eq(BX));  // open: gt, lt
  and DPR (DPR_out, ~BX, ~Funct[5], ~Op[0], ~Op[1]);  // AND_Gate
  and DPI (DPI_out, ~BX, Funct[5], ~Op[0], ~Op[1]);  // AND_Gate
  and STR (MemW, ~BX, ~Funct[0], Op[0], ~Op[1]);  // AND_Gate
  and LDR (MemtoReg, ~BX, Funct[0], Op[0], ~Op[1]);  // AND_Gate
  and B (Branch, ~BX, ~Op[0], Op[1]);  // AND_Gate
  and and_1 (BL, Funct[4], Branch);
  or or_1 (RegSrc[0], BL, Branch, BX);
  or or_2 (ImmSrc[0], MemW, MemtoReg);
  or or_3 (RegW, BL, DPR_out, DPI_out, MemtoReg, BX);
  or or_4 (AluSrc, Branch, MemtoReg, MemW, DPI_out);
  or or_5 (ALUop, DPI_out, DPR_out);

  assign ImmSrc[1] = Branch;
  assign RegSrc[1] = MemW;
endmodule

module ALU_Decoder (
  input  [4:0] Funct,
  input  ALU_Op,
  output MOV,
  output [1:0] ALU_Control,
  output [1:0] FlagW,
  output CMP
);

  wire ADD1_out, AND0_out, AND1_out, ORR0_out, ORR1_out, SUB0_out, SUB1_out;

  and ADD1 (ADD1_out, ALU_Op, ~Funct[4], Funct[3], ~Funct[2], ~Funct[1], Funct[0]);  // AND_Gate
  and SUB0 (SUB0_out, ALU_Op, ~Funct[4], ~Funct[3], Funct[2], ~Funct[1], ~Funct[0]);  // AND_Gate
  and SUB1 (SUB1_out, ALU_Op, ~Funct[4], ~Funct[3], Funct[2], ~Funct[1], Funct[0]);  // AND_Gate
  and AND0 (AND0_out, ALU_Op, ~Funct[4], ~Funct[3], ~Funct[2], ~Funct[1], ~Funct[0]);  // AND_Gate
  and AND1 (AND1_out, ALU_Op, ~Funct[4], ~Funct[3], ~Funct[2], ~Funct[1], Funct[0]);  // AND_Gate
  or ALUControl0 (ALU_Control[0], SUB0_out, SUB1_out, ORR0_out, ORR1_out, CMP);
  or ALUControl1 (ALU_Control[1], AND0_out, AND1_out, ORR0_out, ORR1_out);
  or FlagW_0 (FlagW[0], ADD1_out, SUB1_out, CMP);
  or FlagW_1 (FlagW[1], ADD1_out, SUB1_out, AND1_out, ORR1_out, CMP);
  and ORR0 (ORR0_out, ALU_Op, Funct[4], Funct[3], ~Funct[2], ~Funct[1], ~Funct[0]);  // AND_Gate
  and ORR1 (ORR1_out, ALU_Op, Funct[4], Funct[3], ~Funct[2], ~Funct[1], Funct[0]);  // AND_Gate
  and u_CMP (CMP, ALU_Op, Funct[4], ~Funct[3], Funct[2], ~Funct[1], Funct[0]);  // AND_Gate
  and u_MOV (MOV, ALU_Op, Funct[4], Funct[3], ~Funct[2], Funct[1], ~Funct[0]);  // AND_Gate
endmodule

module Register_File (
  input  [31:0] WD3,
  input  clk,
  input  clr,
  input  WE3,
  input  [3:0] A3,
  input  [3:0] A1,
  input  [3:0] A2,
  input  [31:0] R15,
  output [31:0] RD1,
  output [31:0] RD2,
  output [31:0] R0,
  output [31:0] R1,
  output [31:0] R2,
  output [31:0] R3,
  output [31:0] R4,
  output [31:0] R5,
  output [31:0] R6,
  output [31:0] R7,
  output [31:0] R8,
  output [31:0] R9,
  output [31:0] R10,
  output [31:0] R11,
  output [31:0] R12,
  output [31:0] R13,
  output [31:0] R14
);

  wire decoder_1_out0, decoder_1_out1, decoder_1_out2, decoder_1_out3, decoder_1_out4, decoder_1_out5,
       decoder_1_out6, decoder_1_out7, decoder_1_out8, decoder_1_out9, decoder_1_out10, decoder_1_out11,
       decoder_1_out12, decoder_1_out13, decoder_1_out14;

  Decoder_part #(.select(4), .disabled(0)) decoder_1 (
    .out0(decoder_1_out0), .out1(decoder_1_out1), .out2(decoder_1_out2), .out3(decoder_1_out3),
    .out4(decoder_1_out4), .out5(decoder_1_out5), .out6(decoder_1_out6), .out7(decoder_1_out7),
    .out8(decoder_1_out8), .out9(decoder_1_out9), .out10(decoder_1_out10), .out11(decoder_1_out11),
    .out12(decoder_1_out12), .out13(decoder_1_out13), .out14(decoder_1_out14), .sel(A3), .en(WE3));  // open: out15
  Register #(.width(32)) u_R0 (.D(WD3), .en(decoder_1_out0), .Q(R0), .clk(clk), .clr(clr));
  Register #(.width(32)) u_R1 (.D(WD3), .en(decoder_1_out1), .Q(R1), .clk(clk), .clr(clr));
  Register #(.width(32)) u_R2 (.D(WD3), .en(decoder_1_out2), .Q(R2), .clk(clk), .clr(clr));
  Register #(.width(32)) u_R3 (.D(WD3), .en(decoder_1_out3), .Q(R3), .clk(clk), .clr(clr));
  Register #(.width(32)) u_R4 (.D(WD3), .en(decoder_1_out4), .Q(R4), .clk(clk), .clr(clr));
  Register #(.width(32)) u_R5 (.D(WD3), .en(decoder_1_out5), .Q(R5), .clk(clk), .clr(clr));
  Register #(.width(32)) u_R6 (.D(WD3), .en(decoder_1_out6), .Q(R6), .clk(clk), .clr(clr));
  Register #(.width(32)) u_R7 (.D(WD3), .en(decoder_1_out7), .Q(R7), .clk(clk), .clr(clr));
  Register #(.width(32)) u_R8 (.D(WD3), .en(decoder_1_out8), .Q(R8), .clk(clk), .clr(clr));
  Register #(.width(32)) u_R9 (.D(WD3), .en(decoder_1_out9), .Q(R9), .clk(clk), .clr(clr));
  Register #(.width(32)) u_R10 (.D(WD3), .en(decoder_1_out10), .Q(R10), .clk(clk), .clr(clr));
  Register #(.width(32)) u_R11 (.D(WD3), .en(decoder_1_out11), .Q(R11), .clk(clk), .clr(clr));
  Register #(.width(32)) u_R12 (.D(WD3), .en(decoder_1_out12), .Q(R12), .clk(clk), .clr(clr));
  Register #(.width(32)) u_R13 (.D(WD3), .en(decoder_1_out13), .Q(R13), .clk(clk), .clr(clr));
  Register #(.width(32)) u_R14 (.D(WD3), .en(decoder_1_out14), .Q(R14), .clk(clk), .clr(clr));
  Multiplexer #(.select(4), .width(32), .enable("false")) multiplexer_1 (
    .in0(R0), .in1(R1), .in2(R2), .in3(R3), .in4(R4), .in5(R5), .in6(R6), .in7(R7), .in8(R8), .in9(R9),
    .in10(R10), .in11(R11), .in12(R12), .in13(R13), .in14(R14), .in15(R15), .out(RD1), .sel(A1));
  Multiplexer #(.select(4), .width(32), .enable("false")) multiplexer_2 (
    .in0(R0), .in1(R1), .in2(R2), .in3(R3), .in4(R4), .in5(R5), .in6(R6), .in7(R7), .in8(R8), .in9(R9),
    .in10(R10), .in11(R11), .in12(R12), .in13(R13), .in14(R14), .in15(R15), .out(RD2), .sel(A2));
endmodule

module Instruction_Memory (
  input  [1:0] in_1,
  input  [31:0] A,
  output [31:0] RD
);

  wire [7:0] demultiplexer_1_out0, demultiplexer_1_out1, demultiplexer_1_out2, demultiplexer_1_out3;
  wire [31:0] rom_1_data, rom_2_data, rom_3_data, rom_4_data;

  Demultiplexer #(.select(2), .width(8), .enable("false")) demultiplexer_1 (
    .out0(demultiplexer_1_out0), .out1(demultiplexer_1_out1), .out2(demultiplexer_1_out2),
    .out3(demultiplexer_1_out3), .in(A[9:2]), .sel(in_1));
  ROM #(.dataWidth(32)) rom_1 (.addr(demultiplexer_1_out0), .data(rom_1_data), .sel(1'b1));
  ROM #(.dataWidth(32)) rom_2 (.addr(demultiplexer_1_out1), .data(rom_2_data), .sel(1'b1));
  ROM #(.dataWidth(32)) rom_3 (.addr(demultiplexer_1_out2), .data(rom_3_data), .sel(1'b1));
  ROM #(.dataWidth(32)) rom_4 (.addr(demultiplexer_1_out3), .data(rom_4_data), .sel(1'b1));
  Multiplexer #(.select(2), .width(32), .enable("false")) multiplexer_1 (
    .in0(rom_1_data), .in1(rom_2_data), .in2(rom_3_data), .in3(rom_4_data), .out(RD), .sel(in_1));

  // Notes on the sheet:
  //   fib iter
  //   contents of rom_1 (hex, n*v repeats v):
  //   e3a0000a eb000000 eafffffe e3500000 a00000c e3500001 a00000c e3a01000 e3a02001 e3a03000 e3a0c001
  //   e15c0000 ca000008 e0813002 e1a01002 e1a02003 e28cc001 eafffff8 e3a03000 ea000001 e3a03001 eaffffff
  //   e1a00003 e12fff1e
  //   fib rec
  //   find max
  //   sum array
  //   contents of rom_2 (hex, n*v repeats v):
  //   e3a0d901 e3a0000a eb000000 eafffffe e24dd004 e58d4000 e24dd004 e58d5000 e24dd004 e58de000 e3500000
  //   a000008 e3500001 a000006 e1a04000 e2400001 ebfffff2 e1a05000 e2440002 ebffffef e0800005 e59de000
  //   e28dd004 e59d5000 e28dd004 e59d4000 e28dd004 e12fff1e
  //   contents of rom_4 (hex, n*v repeats v):
  //   e3a0d901 e3a00003 eb000000 eafffffe e24dd004 e58d4000 e24dd004 e58d5000 e24dd004 e58de000 e3500000
  //   a000008 e3500001 a000006 e1a04000 e2400001 ebfffff2 e1a05000 e2440002 ebffffef e0800005 e59de000
  //   e28dd004 e59d5000 e28dd004 e59d4000 e28dd004 e12fff1e
endmodule

module Data_Memory (
  input  [31:0] A,
  input  [31:0] WD,
  input  clk,
  input  WE,
  input  clr,
  output [31:0] RD
);

  wire not_1_out;

  RAM #(.dataWidth(32), .bus("separate")) ram_1 (
    .addr(A[9:2]), .din(WD), .data(RD), .str(WE), .sel(1'b1), .clk(clk), .ld(not_1_out), .clr(clr));
  not not_1 (not_1_out, WE);
endmodule

module ALU (
  input  [31:0] A,
  input  [31:0] B,
  input  [1:0] ALU_Control,
  output [31:0] Aout,
  output [31:0] ALUResult,
  output [3:0] ALU_Flags
);

  wire adder_1_cout, not_1_out, or_2_out, subtractor_1_bout, xnor_1_out, xor_1_out;
  wire [31:0] adder_1_out, and_1_out, or_1_out, subtractor_1_out;

  Adder #(.width(32)) adder_1 (.a(A), .b(B), .out(adder_1_out), .cout(adder_1_cout));  // open: cin
  Subtractor #(.width(32)) subtractor_1 (.a(A), .b(B), .out(subtractor_1_out), .bout(subtractor_1_bout));  // open: bin
  assign and_1_out = A & B;  // AND_Gate and_1, 32 bits wide
  assign or_1_out = A | B;  // OR_Gate or_1, 32 bits wide
  Multiplexer #(.select(2), .width(32), .disabled(0), .enable("false")) multiplexer_1 (
    .in0(adder_1_out), .in1(subtractor_1_out), .in2(and_1_out), .in3(or_1_out),
    .out({ALU_Flags[3], ALUResult[30:0]}), .sel(ALU_Control));
  NotExactlyOne xnor_1 (.out(xnor_1_out), .in0(ALU_Control[0]), .in1(A[31]), .in2(B[31]));
  Comparator #(.width(32)) comparator_1 (
    .a({ALU_Flags[3], ALUResult[30:0]}), .b({32{1'b0}}), .eq(ALU_Flags[2]));  // open: gt, lt
  xor xor_1 (xor_1_out, A[31], adder_1_out[31]);
  and and_2 (ALU_Flags[0], xnor_1_out, xor_1_out, not_1_out);
  or or_2 (or_2_out, subtractor_1_bout, adder_1_cout);
  not not_1 (not_1_out, ALU_Control[1]);
  and and_3 (ALU_Flags[1], not_1_out, or_2_out);

  assign ALUResult[31] = ALU_Flags[3];
  assign Aout = A;

  // Other names for the same wires on the sheet: ALU_Control_0 = ALU_Control[0]; ALU_Control_1 = ALU_Control[1];
  //   V = ALU_Flags[0]; C = ALU_Flags[1]; Z = ALU_Flags[2]; N = ALU_Flags[3]
endmodule

module Extender (
  input  [23:0] _23_0,
  input  [1:0] ImmSrc,
  output [31:0] ExtImm
);

  wire [23:0] shifter_1_out;
  wire [31:0] bit_extender_1_out, bit_extender_2_out, bit_extender_3_out;

  Shifter #(.width(24)) shifter_1 (.in(_23_0), .\dist (5'b00010), .out(shifter_1_out));
  assign bit_extender_1_out = {{8{shifter_1_out[23]}}, shifter_1_out};  // Bit_Extender bit_extender_1
  assign bit_extender_2_out = {{20{_23_0[11]}}, _23_0[11:0]};  // Bit_Extender bit_extender_2
  assign bit_extender_3_out = {{24{_23_0[7]}}, _23_0[7:0]};  // Bit_Extender bit_extender_3
  Multiplexer #(.select(2), .width(32), .disabled(0), .enable("false")) multiplexer_1 (
    .in0(bit_extender_3_out), .in1(bit_extender_2_out), .in2(bit_extender_1_out), .out(ExtImm), .sel(ImmSrc));  // open: in3
endmodule

module RegID (
  input  [1:0] RegSrc,
  input  BX,
  input  [3:0] RN,
  input  [3:0] RM,
  input  [3:0] RD,
  input  BL,
  output BX_2,
  output [3:0] A1,
  output [3:0] A2,
  output [3:0] A3,
  output BL_2
);

  wire [3:0] multiplexer_1_out;

  Multiplexer #(.width(4), .disabled(0), .enable("false")) multiplexer_1 (
    .in0(RN), .in1(4'b1111), .out(multiplexer_1_out), .sel(RegSrc[0]));
  Multiplexer #(.width(4), .disabled(0), .enable("false")) multiplexer_2 (
    .in0(RM), .in1(RD), .out(A2), .sel(RegSrc[1]));
  Multiplexer #(.width(4), .disabled(0), .enable("false")) multiplexer_3 (
    .in0(multiplexer_1_out), .in1(RM), .out(A1), .sel(BX));
  Multiplexer #(.width(4), .disabled(0), .enable("false")) multiplexer_4 (.in0(RD), .in1(4'b1110), .out(A3), .sel(BL));

  assign BL_2 = BL;
  assign BX_2 = BX;
endmodule

module PCPlus (
  input  [31:0] PC,
  output [31:0] PCPlus8,
  output [31:0] PCPlus4
);

  Adder #(.width(32)) adder_1 (.a(32'h4), .b(PC), .out(PCPlus4), .cin(1'b0));  // open: cout
  Adder #(.width(32)) adder_2 (.a(32'h4), .b(PCPlus4), .out(PCPlus8), .cin(1'b0));  // open: cout
endmodule
